# Fritzing sketch Fritzing (saved by Fritzing 0.9.3b)

parts:
  KY-1 = Keyes Relay [package=THT]
  LED2 = LEDs [package=led10mm]
  Part2 = Lilypad Battery Connect
  HLK-PM1 = HLK-PM01
  U2 = NodeMCU V3.0

nets:
  N1: KY-1.signal, U2.D4
  N2: KY-1.power, U2.3V3
  N3: KY-1.ground, HLK-PM1.-Vo, U2.GND
  N4: KY-1.C, Part2.+, HLK-PM1.AC#0
  N5: KY-1.NO, LED2.C
  N6: LED2.A, Part2.-, HLK-PM1.AC#1
  N7: HLK-PM1.+Vo, U2.Vin

notes:
  230V AC power supply
  Socket Relay
  230v/5v
  Step Down
  Plug:
  1. Ground
  2. 3v
  3. Signal
  4. Signal
  5. 5v
  6. Analog

custom parts:
  Keyes Relay: The Keyes 5V relay module is suitable for SCM development, home appliance control. It uses a 5V~12V TIL control signal which can control DC / AC signal.
  LEDs: LEDs Standard schematic elements and footprints for 5mm, 3mm, 1206, and 0603 sized LEDs. 5mm - Spark Fun Electronics SKU : COM-00529 (and others)
  NodeMCU V3.0: ESP8266 based NodeMCU
